// Logisim project Group6.circ as structural Verilog: 6 circuits, main circuit main
module main (
  input  in_1,
  input  in_2,
  input  in_3
);

  wire k_map_1_a_2, k_map_1_b_2, k_map_1_d, k_map_1_e, k_map_1_f, k_map_1_g, k_map_1_out_6, nand_1_a_2,
       nand_1_b_2, nand_1_c_2, nand_1_d, nand_1_e, nand_1_f, nand_1_g, nor_1_g_a_prime_c_prime, nor_1_out_4,
       nor_1_out_5, nor_1_out_6, nor_1_out_7, nor_1_out_8, nor_1_out_9, pos_1_a, pos_1_b, pos_1_c, pos_1_d,
       pos_1_e, pos_1_f, pos_1_g, sop_1_a_2, sop_1_b_2, sop_1_c_2, sop_1_d, sop_1_e, sop_1_f, sop_1_g;

  POS pos_1 (
    .a(pos_1_a), .b(pos_1_b), .c(pos_1_c), .d(pos_1_d), .e(pos_1_e), .f(pos_1_f), .g(pos_1_g), .in_1(in_1),
    .in_2(in_2), .in_3(in_3));
  K_Map k_map_1 (
    .A(in_1), .B(in_2), .C(in_3), .a_2(k_map_1_a_2), .b_2(k_map_1_b_2), .out_6(k_map_1_out_6), .d(k_map_1_d),
    .e(k_map_1_e), .f(k_map_1_f), .g(k_map_1_g));
  SOP sop_1 (
    .A(in_1), .B(in_2), .C(in_3), .a_2(sop_1_a_2), .b_2(sop_1_b_2), .c_2(sop_1_c_2), .d(sop_1_d),
    .e(sop_1_e), .f(sop_1_f), .g(sop_1_g));
  NAND nand_1 (
    .A(in_1), .B(in_2), .C(in_3), .a_2(nand_1_a_2), .b_2(nand_1_b_2), .c_2(nand_1_c_2), .d(nand_1_d),
    .e(nand_1_e), .f(nand_1_f), .g(nand_1_g));
  NOR nor_1 (
    .in_1(in_1), .in_2(in_2), .in_3(in_3), .out_4(nor_1_out_4), .out_5(nor_1_out_5), .out_6(nor_1_out_6),
    .out_8(nor_1_out_8), .out_9(nor_1_out_9), .g_A_prime_C_prime(nor_1_g_a_prime_c_prime), .out_7(nor_1_out_7));
  _7_Segment_Display u_7_segment_display_1 (
    .g(pos_1_g), .f(pos_1_f), .a(pos_1_a), .b(pos_1_b), .e(pos_1_e), .d(pos_1_d), .c(pos_1_c));  // open: dp
  _7_Segment_Display u_7_segment_display_2 (
    .g(k_map_1_g), .f(k_map_1_f), .a(k_map_1_a_2), .b(k_map_1_b_2), .e(k_map_1_e), .d(k_map_1_d),
    .c(k_map_1_out_6));  // open: dp
  _7_Segment_Display u_7_segment_display_3 (
    .g(sop_1_g), .f(sop_1_f), .a(sop_1_a_2), .b(sop_1_b_2), .e(sop_1_e), .d(sop_1_d), .c(sop_1_c_2));  // open: dp
  _7_Segment_Display u_7_segment_display_4 (
    .g(nand_1_g), .f(nand_1_f), .a(nand_1_a_2), .b(nand_1_b_2), .e(nand_1_e), .d(nand_1_d), .c(nand_1_c_2));  // open: dp
  _7_Segment_Display u_7_segment_display_5 (
    .g(nor_1_g_a_prime_c_prime), .f(nor_1_out_9), .a(nor_1_out_4), .b(nor_1_out_5), .e(nor_1_out_8),
    .d(nor_1_out_7), .c(nor_1_out_6));  // open: dp

  // Notes on the sheet:
  //   Truth Table: 
  //   A     B     C     Represents
  //   0     0     0               5
  //   0     0     1               9
  //   0     1     0               n
  //   0     1     1               A
  //   1     0     0                t
  //   1     0     1                1
  //   1     1     0                4
  //   A      B      C      a      b      c      d      e      f      g
  //   0      0      0      1      0      1      1      0      1      1
  //   0      0      1      1      1      1      1      0      1      1
  //   0      1      0      0      0      1      0      1      0      1
  //   0      1      1      1      1      1      0      1      1      1
  //   1      0      0      0      0      0      1      1      1      1
  //   1      0      1      0      1      1      0      0      0      0
  //   1      1      0      0      1      1      0      0      1      1
endmodule

module POS (
  input  in_1,
  input  in_2,
  input  in_3,
  output a,
  output b,
  output c,
  output d,
  output e,
  output f,
  output g
);

  wire and_1_out, and_2_out, and_3_out, and_4_out, and_5_out, and_6_out, and_7_out, not_1_out, not_2_out,
       not_3_out, or_1_out, or_2_out, or_3_out, or_4_out, or_5_out, or_6_out, or_7_out, or_8_out, or_9_out,
       or_10_out, or_11_out, or_12_out, or_13_out, or_14_out, or_15_out, or_16_out, or_17_out, or_18_out,
       or_19_out, or_20_out, or_21_out, or_22_out, or_23_out, or_24_out, or_25_out, or_26_out, or_28_out,
       or_29_out, or_30_out, or_31_out, or_32_out, or_33_out, or_34_out, or_35_out, or_36_out, or_37_out;

  not not_1 (not_1_out, in_1);
  not not_2 (not_2_out, in_2);
  not not_3 (not_3_out, in_3);
  or or_1 (or_1_out, in_1, not_2_out);
  or or_2 (or_2_out, not_1_out, in_2);
  or or_3 (or_3_out, not_1_out, in_2);
  or or_4 (or_4_out, not_1_out, not_2_out);
  or or_5 (or_5_out, in_1, in_2);
  or or_6 (or_6_out, in_1, not_2_out);
  or or_7 (or_7_out, not_1_out, in_2);
  or or_8 (or_8_out, not_1_out, in_2);
  or or_9 (or_9_out, in_1, not_2_out);
  or or_10 (or_10_out, in_1, not_2_out);
  or or_11 (or_11_out, not_1_out, in_2);
  or or_12 (or_12_out, not_1_out, not_2_out);
  or or_13 (or_13_out, in_1, in_2);
  or or_14 (or_14_out, in_1, in_2);
  or or_15 (or_15_out, not_1_out, in_2);
  or or_16 (or_16_out, not_1_out, not_2_out);
  or or_17 (or_17_out, in_1, not_2_out);
  or or_18 (or_18_out, not_1_out, in_2);
  or or_19 (or_19_out, not_1_out, in_2);
  or or_20 (or_20_out, or_1_out, in_3);
  or or_21 (or_21_out, or_2_out, in_3);
  or or_22 (or_22_out, or_3_out, not_3_out);
  or or_23 (or_23_out, or_4_out, in_3);
  or or_24 (or_24_out, or_5_out, in_3);
  or or_25 (or_25_out, or_6_out, in_3);
  or or_26 (or_26_out, or_7_out, in_3);
  or or_27 (c, or_8_out, in_3);
  or or_28 (or_28_out, or_9_out, in_3);
  or or_29 (or_29_out, or_10_out, not_3_out);
  or or_30 (or_30_out, or_11_out, not_3_out);
  or or_31 (or_31_out, or_12_out, in_3);
  or or_32 (or_32_out, or_13_out, in_3);
  or or_33 (or_33_out, or_14_out, not_3_out);
  or or_34 (or_34_out, or_15_out, not_3_out);
  or or_35 (or_35_out, or_16_out, in_3);
  or or_36 (or_36_out, or_17_out, in_3);
  or or_37 (or_37_out, or_18_out, not_3_out);
  or or_38 (g, or_19_out, not_3_out);
  and and_1 (and_1_out, or_20_out, or_21_out);
  and and_2 (and_2_out, or_22_out, or_23_out);
  and and_3 (and_3_out, or_24_out, or_25_out);
  and and_4 (and_4_out, or_28_out, or_29_out);
  and and_5 (and_5_out, or_30_out, or_31_out);
  and and_6 (and_6_out, or_32_out, or_33_out);
  and and_7 (and_7_out, or_34_out, or_35_out);
  and and_8 (f, or_36_out, or_37_out);
  and and_9 (a, and_1_out, and_2_out);
  and and_10 (b, and_3_out, or_26_out);
  and and_11 (d, and_4_out, and_5_out);
  and and_12 (e, and_6_out, and_7_out);
endmodule

module K_Map (
  input  A,
  input  B,
  input  C,
  output a_2,
  output b_2,
  output out_6,
  output d,
  output e,
  output f,
  output g
);

  wire and_1_out, and_2_out, and_3_out, and_4_out, and_5_out, and_6_out, and_8_out, and_10_out, not_1_out,
       not_2_out, not_3_out, or_1_out, or_2_out, or_4_out, xor_1_out, xor_2_out;

  not not_1 (not_1_out, A);
  not not_2 (not_2_out, B);
  not not_3 (not_3_out, C);
  or or_1 (or_1_out, not_2_out, C);
  and and_1 (and_1_out, not_1_out, C);
  and and_2 (and_2_out, B, not_3_out);
  and and_3 (and_3_out, not_2_out, C);
  xor xor_1 (xor_1_out, B, C);
  or or_2 (or_2_out, not_1_out, not_3_out);
  and and_4 (and_4_out, not_1_out, B);
  and and_5 (and_5_out, not_2_out, not_3_out);
  and and_6 (and_6_out, not_2_out, not_1_out);
  xor xor_2 (xor_2_out, A, C);
  or or_3 (g, not_1_out, not_3_out);
  and and_7 (a_2, or_1_out, not_1_out);
  and and_8 (and_8_out, and_2_out, A);
  or or_4 (or_4_out, and_8_out, and_3_out);
  and and_9 (d, or_2_out, not_2_out);
  or or_5 (e, and_4_out, and_10_out);
  and and_10 (and_10_out, and_5_out, A);
  or or_6 (f, and_6_out, xor_2_out);
  or or_7 (b_2, and_1_out, or_4_out);
  or or_8 (out_6, not_1_out, xor_1_out);

  // Notes on the sheet:
  //   A'
  //   B'
  //   C'
endmodule

module SOP (
  input  A,
  input  B,
  input  C,
  output a_2,
  output b_2,
  output c_2,
  output d,
  output e,
  output f,
  output g
);

  wire and_1_out, and_2_out, and_3_out, and_4_out, and_5_out, and_6_out, and_7_out, and_8_out, and_9_out,
       and_10_out, and_11_out, and_12_out, and_13_out, and_14_out, and_15_out, and_16_out, and_17_out,
       and_18_out, and_19_out, and_20_out, and_21_out, and_22_out, and_23_out, and_24_out, and_25_out,
       and_26_out, and_27_out, not_1_out, not_2_out, not_3_out, or_1_out, or_3_out, or_4_out, or_5_out,
       or_6_out, or_7_out, or_12_out;

  not not_1 (not_1_out, A);
  not not_2 (not_2_out, B);
  not not_3 (not_3_out, C);
  and and_1 (and_1_out, not_1_out, not_2_out);
  and and_2 (and_2_out, A, not_2_out);
  and and_3 (and_3_out, and_1_out, not_3_out);
  and and_4 (and_4_out, and_1_out, C);
  and and_5 (and_5_out, not_1_out, B);
  and and_6 (and_6_out, and_2_out, C);
  and and_7 (and_7_out, A, B);
  and and_8 (and_8_out, and_7_out, not_3_out);
  and and_9 (and_9_out, not_1_out, not_2_out);
  and and_10 (and_10_out, and_9_out, not_3_out);
  and and_11 (and_11_out, not_1_out, B);
  and and_12 (and_12_out, A, not_2_out);
  and and_13 (and_13_out, not_1_out, B);
  and and_14 (and_14_out, not_1_out, B);
  and and_15 (and_15_out, A, not_2_out);
  and and_16 (and_16_out, not_1_out, B);
  and and_17 (and_17_out, and_16_out, C);
  and and_18 (and_18_out, A, B);
  and and_19 (and_19_out, and_18_out, not_3_out);
  and and_20 (and_20_out, not_1_out, B);
  and and_21 (and_21_out, and_20_out, not_3_out);
  or or_1 (or_1_out, and_3_out, and_4_out);
  or or_2 (a_2, or_1_out, and_22_out);
  and and_22 (and_22_out, and_5_out, C);
  or or_3 (or_3_out, and_22_out, and_4_out);
  or or_4 (or_4_out, and_6_out, and_8_out);
  or or_5 (or_5_out, b_2, and_10_out);
  and and_23 (and_23_out, and_11_out, not_3_out);
  or or_6 (or_6_out, and_10_out, and_4_out);
  and and_24 (and_24_out, and_12_out, not_3_out);
  and and_25 (and_25_out, and_13_out, not_3_out);
  and and_26 (and_26_out, and_14_out, C);
  and and_27 (and_27_out, and_15_out, not_3_out);
  or or_7 (or_7_out, and_17_out, and_19_out);
  or or_8 (g, and_21_out, f);
  or or_9 (b_2, or_3_out, or_4_out);
  or or_10 (c_2, or_5_out, and_23_out);
  or or_11 (d, or_6_out, and_24_out);
  or or_12 (or_12_out, and_25_out, and_26_out);
  or or_13 (e, or_12_out, and_27_out);
  or or_14 (f, d, or_7_out);

  // Notes on the sheet:
  //   A'
  //   B'
  //   C'
endmodule

module NAND (
  input  A,
  input  B,
  input  C,
  output a_2,
  output b_2,
  output c_2,
  output d,
  output e,
  output f,
  output g
);

  wire nand_1_out, nand_2_out, nand_3_out, nand_4_out, nand_5_out, nand_6_out, nand_7_out, nand_8_out,
       nand_9_out, nand_10_out, nand_11_out, nand_13_out, nand_14_out, nand_15_out, nand_16_out, nand_17_out,
       nand_18_out, nand_19_out, nand_20_out, nand_21_out, nand_24_out, nand_25_out, nand_27_out, nand_28_out;

  nand nand_1 (nand_1_out, A, A);
  nand nand_2 (nand_2_out, B, B);
  nand nand_3 (nand_3_out, C, C);
  nand nand_4 (nand_4_out, B, nand_3_out);
  nand nand_5 (nand_5_out, A, B);
  nand nand_6 (nand_6_out, A, C);
  nand nand_7 (nand_7_out, A, nand_2_out);
  nand nand_8 (nand_8_out, nand_1_out, B);
  nand nand_9 (nand_9_out, nand_1_out, C);
  nand nand_10 (nand_10_out, A, nand_3_out);
  nand nand_11 (nand_11_out, nand_1_out, nand_2_out);
  nand nand_12 (g, A, C);
  nand nand_13 (nand_13_out, nand_4_out, nand_1_out);
  nand nand_14 (nand_14_out, nand_5_out, C);
  nand nand_15 (nand_15_out, nand_5_out, nand_5_out);
  nand nand_16 (nand_16_out, nand_2_out, C);
  nand nand_17 (nand_17_out, nand_16_out, nand_18_out);
  nand nand_18 (nand_18_out, B, nand_3_out);
  nand nand_19 (nand_19_out, nand_6_out, nand_2_out);
  nand nand_20 (nand_20_out, nand_7_out, nand_7_out);
  nand nand_21 (nand_21_out, nand_9_out, nand_10_out);
  nand nand_22 (a_2, nand_13_out, nand_13_out);
  nand nand_23 (b_2, nand_14_out, nand_24_out);
  nand nand_24 (nand_24_out, nand_15_out, nand_3_out);
  nand nand_25 (nand_25_out, nand_17_out, nand_17_out);
  nand nand_26 (d, nand_19_out, nand_19_out);
  nand nand_27 (nand_27_out, nand_20_out, nand_3_out);
  nand nand_28 (nand_28_out, nand_21_out, nand_21_out);
  nand nand_29 (c_2, nand_25_out, A);
  nand nand_30 (e, nand_27_out, nand_8_out);
  nand nand_31 (f, nand_28_out, nand_11_out);

  // Notes on the sheet:
  //   A'
  //   B'
  //   C'
endmodule

module NOR (
  input  in_1,
  input  in_2,
  input  in_3,
  output out_4,
  output out_5,
  output out_6,
  output out_7,
  output out_8,
  output out_9,
  output g_A_prime_C_prime
);

  wire nor_1_out, nor_2_out, nor_3_out, nor_4_out, nor_5_out, nor_6_out, nor_7_out, nor_8_out, nor_9_out,
       nor_10_out, nor_11_out, nor_12_out, nor_13_out, nor_14_out, nor_16_out, nor_17_out, nor_18_out,
       nor_20_out, nor_21_out, nor_22_out, nor_24_out, nor_25_out, nor_26_out, nor_27_out, nor_28_out,
       nor_29_out, nor_30_out, nor_33_out;

  nor nor_1 (nor_1_out, in_1, in_1);
  nor nor_2 (nor_2_out, in_2, in_2);
  nor nor_3 (nor_3_out, in_3, in_3);
  nor nor_4 (nor_4_out, nor_2_out, in_3);
  nor nor_5 (nor_5_out, nor_1_out, nor_2_out);
  nor nor_6 (nor_6_out, nor_1_out, nor_2_out);
  nor nor_7 (nor_7_out, in_2, nor_3_out);
  nor nor_8 (nor_8_out, nor_2_out, in_3);
  nor nor_9 (nor_9_out, nor_1_out, nor_3_out);
  nor nor_10 (nor_10_out, nor_1_out, in_2);
  nor nor_11 (nor_11_out, in_1, in_2);
  nor nor_12 (nor_12_out, nor_1_out, in_3);
  nor nor_13 (nor_13_out, in_1, nor_3_out);
  nor nor_14 (nor_14_out, nor_1_out, nor_3_out);
  nor nor_15 (out_4, nor_4_out, in_1);
  nor nor_16 (nor_16_out, nor_5_out, nor_3_out);
  nor nor_17 (nor_17_out, nor_6_out, nor_6_out);
  nor nor_18 (nor_18_out, nor_7_out, nor_8_out);
  nor nor_19 (out_7, in_2, nor_9_out);
  nor nor_20 (nor_20_out, in_1, nor_2_out);
  nor nor_21 (nor_21_out, nor_10_out, nor_10_out);
  nor nor_22 (nor_22_out, nor_12_out, nor_13_out);
  nor nor_23 (g_A_prime_C_prime, nor_14_out, nor_14_out);
  nor nor_24 (nor_24_out, nor_17_out, in_3);
  nor nor_25 (nor_25_out, nor_18_out, nor_18_out);
  nor nor_26 (nor_26_out, nor_21_out, in_3);
  nor nor_27 (nor_27_out, nor_22_out, nor_22_out);
  nor nor_28 (nor_28_out, nor_16_out, nor_24_out);
  nor nor_29 (nor_29_out, nor_25_out, nor_1_out);
  nor nor_30 (nor_30_out, nor_20_out, nor_26_out);
  nor nor_31 (out_6, nor_29_out, nor_29_out);
  nor nor_32 (out_8, nor_30_out, nor_30_out);
  nor nor_33 (nor_33_out, nor_11_out, nor_27_out);
  nor nor_34 (out_5, nor_28_out, nor_28_out);
  nor nor_35 (out_9, nor_33_out, nor_33_out);

  // Notes on the sheet:
  //   a=A'(B'+C)
  //   d=B'(A'+C')
  //   b=C(A'+B')+ABC'
  //   c=A'+(B'C+BC')
  //   e=A'B+AB'C'
  //   f=A'B'+A'C+AC'
endmodule
